// Logisim project processtinator.circ as structural Verilog: 1 circuit, main circuit main
module main (
);

  wire and_1_out, clock_1_out, comparator_1_eq, comparator_1_gt, comparator_2_eq, demultiplexer_1_out0,
       demultiplexer_1_out1, demultiplexer_1_out2, demultiplexer_1_out3, demultiplexer_1_out4,
       demultiplexer_1_out5, demultiplexer_1_out6, demultiplexer_1_out7, demultiplexer_1_out12,
       demultiplexer_1_out13, demultiplexer_1_out14, demultiplexer_1_out15, or_1_out, t_ff_1_q, t_ff_2_q;
  wire [3:0] IR_q_2;
  wire [6:0] register_1_q;
  wire [23:0] AR_q, INSCNT_q, multiplexer_1_out, PC_q;
  wire [27:0] IR_q;
  wire [31:0] A_q, adder_1_out, and_2_out, B_q, bit_extender_1_out, bit_extender_2_out, bit_extender_3_out,
       bit_extender_4_out, C_q, D_q, E_q, F_q, G_q, H_q, MR_q, multiplexer_2_out, multiplexer_3_out,
       multiplexer_4_out, negator_1_out, or_2_out, ram_1_dout, shifter_1_out, shifter_2_out;

  Clock clock_1 (.out(clock_1_out));
  Counter #(.width(24), .max('hffffff), .ongoal("stay"), .trigger("falling")) INSCNT (
    .clk(t_ff_2_q), .Q(INSCNT_q));  // open: clr, load, up, count, D, carry
  T_Flip_Flop t_ff_1 (.T(1'b1), .clk(clock_1_out), .Q(t_ff_1_q));  // open: Qn, reset, preset
  T_Flip_Flop #(.trigger("falling")) t_ff_2 (.T(1'b1), .clk(clock_1_out), .Q(t_ff_2_q));  // open: Qn, reset, preset
  // Digital_Oscilloscope digital_oscilloscope_1: pin names not known; wires that end beside it: clock_1_out, clock_1_out, t_ff_1_q, t_ff_2_q
  // Probe on INSCNT_q
  Counter #(.width(24), .max('hffffff), .trigger("falling")) PC (
    .load(demultiplexer_1_out15), .clk(t_ff_2_q), .D(multiplexer_4_out[23:0]), .Q(PC_q));  // open: clr, up, count, carry
  Register #(.width(24)) AR (
    .D(multiplexer_4_out[23:0]), .en(demultiplexer_1_out14), .clk(t_ff_1_q), .Q(AR_q));  // open: clr
  RAM #(.addrWidth(24), .dataWidth(32), .databus("bibus")) ram_1 (
    .addr(multiplexer_1_out), .we(and_1_out), .clk(clock_1_out), .din(multiplexer_4_out), .dout(ram_1_dout));  // open: oe
  Multiplexer #(.width(24), .enable("false")) multiplexer_1 (
    .in0(PC_q), .in1(AR_q), .out(multiplexer_1_out), .sel(t_ff_2_q));
  and and_1 (and_1_out, t_ff_2_q, demultiplexer_1_out12);
  Register #(.width(32)) IR (.D(ram_1_dout), .en(t_ff_2_q), .clk(t_ff_2_q), .Q({IR_q_2, IR_q}));  // open: clr
  Register #(.width(32)) MR (.D(ram_1_dout), .en(t_ff_1_q), .clk(t_ff_1_q), .Q(MR_q));  // open: clr
  Demultiplexer #(.select(4), .enable("false")) demultiplexer_1 (
    .out0(demultiplexer_1_out0), .out1(demultiplexer_1_out1), .out2(demultiplexer_1_out2),
    .out3(demultiplexer_1_out3), .out4(demultiplexer_1_out4), .out5(demultiplexer_1_out5),
    .out6(demultiplexer_1_out6), .out7(demultiplexer_1_out7), .out12(demultiplexer_1_out12),
    .out13(demultiplexer_1_out13), .out14(demultiplexer_1_out14), .out15(demultiplexer_1_out15),
    .in(or_1_out), .sel(IR_q_2));  // open: out8, out9, out10, out11
  // Probe on IR_q_2
  assign bit_extender_1_out = {{16{1'b0}}, IR_q[15:0]};  // Bit_Extender bit_extender_1
  assign bit_extender_2_out = {{8{1'b0}}, PC_q};  // Bit_Extender bit_extender_2
  Register #(.width(32)) A (.D(multiplexer_4_out), .en(demultiplexer_1_out0), .clk(t_ff_1_q), .Q(A_q));  // open: clr
  Register #(.width(32)) B (.D(multiplexer_4_out), .en(demultiplexer_1_out1), .clk(t_ff_1_q), .Q(B_q));  // open: clr
  Register #(.width(32)) C (.D(multiplexer_4_out), .en(demultiplexer_1_out2), .clk(t_ff_1_q), .Q(C_q));  // open: clr
  Register #(.width(32)) D (.D(multiplexer_4_out), .en(demultiplexer_1_out3), .clk(t_ff_1_q), .Q(D_q));  // open: clr
  Register #(.width(32)) E (.D(multiplexer_4_out), .en(demultiplexer_1_out4), .clk(t_ff_1_q), .Q(E_q));  // open: clr
  Register #(.width(32)) F (.D(multiplexer_4_out), .en(demultiplexer_1_out5), .clk(t_ff_1_q), .Q(F_q));  // open: clr
  Register #(.width(32)) G (.D(multiplexer_4_out), .en(demultiplexer_1_out6), .clk(t_ff_1_q), .Q(G_q));  // open: clr
  Register #(.width(32)) H (.D(multiplexer_4_out), .en(demultiplexer_1_out7), .clk(t_ff_1_q), .Q(H_q));  // open: clr
  Multiplexer #(.select(4), .width(32), .enable("false")) multiplexer_2 (
    .in0(A_q), .in1(B_q), .in2(C_q), .in3(D_q), .in4(E_q), .in5(F_q), .in6(G_q), .in7(H_q), .in12(MR_q),
    .in13({32{1'b0}}), .in14(bit_extender_1_out), .in15(bit_extender_2_out), .out(multiplexer_2_out),
    .sel(IR_q[19:16]));  // open: in8, in9, in10, in11
  Multiplexer #(.select(4), .width(32), .enable("false")) multiplexer_3 (
    .in0(A_q), .in1(B_q), .in2(C_q), .in3(D_q), .in4(E_q), .in5(F_q), .in6(G_q), .in7(H_q), .in12(MR_q),
    .in13({32{1'b0}}), .in14(bit_extender_1_out), .in15(bit_extender_2_out), .out(multiplexer_3_out),
    .sel(IR_q[23:20]));  // open: in8, in9, in10, in11
  Register #(.width(7)) register_1 (
    .D(multiplexer_4_out[6:0]), .en(demultiplexer_1_out13), .clk(t_ff_1_q), .Q(register_1_q), .clr(t_ff_2_q));
  // Probe on multiplexer_2_out
  // Probe on IR_q[19:16]
  // Probe on multiplexer_3_out
  // Probe on IR_q[23:20]
  // Probe on IR_q[27:24]
  // Probe on multiplexer_4_out
  TTY tty_1 (.data(register_1_q), .clk(t_ff_2_q), .clr(1'b0));  // open: we
  Adder #(.width(32)) adder_1 (.a(multiplexer_2_out), .b(multiplexer_3_out), .out(adder_1_out));  // open: cin, cout
  Shifter #(.width(32), .shift("lr")) shifter_1 (
    .in(multiplexer_2_out), .\dist (multiplexer_3_out[4:0]), .out(shifter_1_out));
  Shifter #(.width(32)) shifter_2 (.in(multiplexer_2_out), .\dist (multiplexer_3_out[4:0]), .out(shifter_2_out));
  Negator #(.width(32)) negator_1 (.in(multiplexer_2_out), .out(negator_1_out));
  Multiplexer #(.select(3), .width(32), .enable("false")) multiplexer_4 (
    .in0(adder_1_out), .in1(negator_1_out), .in2(and_2_out), .in3(or_2_out), .in4(bit_extender_3_out),
    .in5(bit_extender_4_out), .in6(shifter_2_out), .in7(shifter_1_out), .out(multiplexer_4_out),
    .sel(IR_q[26:24]));
  assign and_2_out = multiplexer_2_out & multiplexer_3_out;  // AND_Gate and_2, 32 bits wide
  or or_1 (or_1_out, ~IR_q[27], ~comparator_2_eq);  // OR_Gate
  Comparator #(.width(32)) comparator_1 (
    .a(multiplexer_2_out), .b(multiplexer_3_out), .gt(comparator_1_gt), .eq(comparator_1_eq));  // open: lt
  assign or_2_out = multiplexer_2_out | multiplexer_3_out;  // OR_Gate or_2, 32 bits wide
  assign bit_extender_3_out = {{31{1'b0}}, comparator_1_eq};  // Bit_Extender bit_extender_3
  assign bit_extender_4_out = {{31{1'b0}}, comparator_1_gt};  // Bit_Extender bit_extender_4
  Comparator #(.width(32)) comparator_2 (.a(multiplexer_2_out), .b({32{1'b0}}), .eq(comparator_2_eq));  // open: gt, lt

  // Notes on the sheet:
  //   A
  //   B
  //   C
  //   D
  //   E
  //   F
  //   G
  //   H
  //   M(em)
  //   N (ull)
  //   O (imm)
  //   P(C)
  //   IMM
  //   SRC1
  //   SRC2
  //   OP
  //   DST
endmodule
